# Fritzing sketch StationMeteo (saved by Fritzing 0.9.4)
stripboards: 1

parts:
  WeMos_D1_Mini1 = WeMos D1 Mini

nets:
  3V3: WeMos_D1_Mini1.3V3, WeMos_D1_Mini1.5V
  N1: WeMos_D1_Mini1.A0, WeMos_D1_Mini1.RX
  N2: WeMos_D1_Mini1.D0, WeMos_D1_Mini1.D1
  N3: WeMos_D1_Mini1.D2, WeMos_D1_Mini1.D5
  N4: WeMos_D1_Mini1.D3, WeMos_D1_Mini1.D6
  N5: WeMos_D1_Mini1.D4, WeMos_D1_Mini1.D7
  N6: WeMos_D1_Mini1.D8, WeMos_D1_Mini1.G
  N7: WeMos_D1_Mini1.RST, WeMos_D1_Mini1.TX

custom parts:
  WeMos D1 Mini: The D1 mini is a mini wifi board based on ESP-8266EX.
